# Fritzing sketch Untitled Sketch (saved by Fritzing 0.7.12b)
breadboards: 1

parts:
  Arduino1 = Arduino
  DS1 = DS18B20 1-Wire Temperature Sensor [part_number=DS18B20]
  R1 = Resistor [tolerance=±5% resistance=4.7k package=THT]
  SSR = Screw terminal [package=THT]
  J1 = Piezo Speaker

nets:
  N1: Arduino1.D11, J1.pin2
  N2: Arduino1.D3, SSR.pin2
  N3: Arduino1.D2, DS1.DQ, R1.Pin_1
  N4: DS1.GND, R1.Pin_0, J1.pin1
  N5: DS1.VDD, SSR.pin1
